// Logisim project 1-bit Register.circ as structural Verilog: 1 circuit, main circuit 1-bit Register
module _1_bit_Register (
  input  CLK,
  input  INPUT,
  output OUTPUT
);

  D_Flip_Flop d_ff_1 (.clk(CLK), .D(INPUT), .Q(OUTPUT));  // open: Qn, preset, en, reset
endmodule
