// Logisim project 12-bit Register.circ as structural Verilog: 1 circuit, main circuit 12-bit Register
module _12_bit_Register (
  input  LD,
  input  [11:0] INP,
  input  INR,
  input  CLK,
  input  CLR,
  output [11:0] OUT
);

  wire d_ff_1_q;

  Pull_Resistor pull_resistor_1 (.node(INR));
  Counter #(.width(12), .max('hfff)) counter_1 (
    .load(LD), .D(INP), .count(INR), .Q(OUT), .clk(CLK), .clr(d_ff_1_q));  // open: carry
  D_Flip_Flop d_ff_1 (.clk(CLK), .D(CLR), .Q(d_ff_1_q), .reset(d_ff_1_q));  // open: Qn, preset, en
  Pull_Resistor pull_resistor_2 (.node(CLR));
endmodule
