// Logisim project 16-bit Register.circ as structural Verilog: 1 circuit, main circuit 16-bit Register
module _16_bit_Register (
  input  LD,
  input  [15:0] INP,
  input  INR,
  input  CLK,
  input  CLR,
  output [15:0] OUT
);

  wire d_ff_1_q;

  Pull_Resistor pull_resistor_1 (.node(INR));
  Counter #(.width(16), .max('hffff)) counter_1 (
    .load(LD), .D(INP), .count(INR), .Q(OUT), .clk(CLK), .clr(d_ff_1_q));  // open: carry
  D_Flip_Flop d_ff_1 (.clk(CLK), .D(CLR), .Q(d_ff_1_q), .reset(d_ff_1_q));  // open: Qn, preset, en
  Pull_Resistor pull_resistor_2 (.node(CLR));
endmodule
