// Logisim project ALU.circ as structural Verilog: 1 circuit, main circuit ALU
module ALU (
  input  [15:0] AC,
  input  [15:0] DR,
  input  Eout,
  input  [2:0] in_4,
  output [15:0] AC_2,
  output Ein
);

  wire Ein1, Ein4, Ein5, not_2_out, xor_1_out;
  wire [15:0] adder_1_out, and_1_out, not_1_out, shifter_1_out, shifter_2_out;
  wire [16:0] bit_extender_1_out, bit_extender_2_out;

  Pull_Resistor pull_resistor_1 (.node(Eout));
  assign bit_extender_1_out = {{1{Eout}}, AC};  // Bit_Extender bit_extender_1
  Pull_Resistor pull_resistor_2 (.node(Eout));
  assign bit_extender_2_out = {{1{Eout}}, AC};  // Bit_Extender bit_extender_2
  Adder #(.width(16)) adder_1 (.a(AC), .b(DR), .out(adder_1_out), .cout(Ein1));  // open: cin
  assign not_1_out = ~AC;  // NOT_Gate not_1, 16 bits wide
  Shifter #(.width(17), .shift("rr")) shifter_1 (
    .in(bit_extender_1_out), .\dist (5'b00001), .out({Ein4, shifter_1_out}));
  Shifter #(.width(17), .shift("rl")) shifter_2 (
    .in(bit_extender_2_out), .\dist (5'b00001), .out({Ein5, shifter_2_out}));
  assign and_1_out = AC & DR;  // AND_Gate and_1, 16 bits wide
  xor xor_1 (xor_1_out, Eout, Ein1);
  Multiplexer #(.select(3), .width(16), .enable("false")) multiplexer_1 (
    .in0(and_1_out), .in1(adder_1_out), .in2(DR), .in3(not_1_out), .in4(shifter_1_out), .in5(shifter_2_out),
    .out(AC_2), .sel(in_4));  // open: in6, in7
  Multiplexer #(.select(3), .enable("false")) multiplexer_2 (
    .in0(Eout), .in1(xor_1_out), .in2(Eout), .in3(Eout), .in4(Ein4), .in5(Ein5), .in6(1'b0), .in7(not_2_out),
    .out(Ein), .sel(in_4));
  not not_2 (not_2_out, Eout);
endmodule
