// Logisim project BUS.circ as structural Verilog: 1 circuit, main circuit BUS
module BUS (
  input  [15:0] in_1,
  input  [15:0] in_2,
  input  [15:0] in_3,
  input  [15:0] in_4,
  input  [15:0] in_5,
  input  [15:0] in_6,
  input  [15:0] in_7,
  input  S0,
  input  S1,
  input  S2,
  output [15:0] out_11
);

  Multiplexer #(.select(3), .width(16)) multiplexer_1 (
    .in1(in_1), .in2(in_2), .in3(in_3), .in4(in_4), .in5(in_5), .in6(in_6), .in7(in_7), .out(out_11),
    .sel({S2, S1, S0}));  // open: in0, en
endmodule
