// Logisim project Basic Computer.circ as structural Verilog: 1 circuit, main circuit Basic Computer
module Basic_Computer (
);

  wire ALU_ein, CLK, CLR_AC, Eout, INR_AC, INR_AR, INR_DR, INR_PC, LD_AC, LD_AR, LD_DR, LD_IR, LD_PC,
       Memory_Enable, S, x1, x2, x3, x4, x5, x6, x7, y0, y1, y2, y3, y4, y5, y6, y7;
  wire [2:0] priority_encoder_1_out, priority_encoder_2_out;
  wire [11:0] AR_out, bit_extender_1_out, bit_extender_2_out, PC_out;
  wire [15:0] AC, ALU_ac_2, bit_extender_3_out, bit_extender_4_out, bus_1_out_11, DR, IR,
       Memory_Control_memory, TR_out;

  Control_Unit Control_Unit (
    .x1(x1), .x2(x2), .x3(x3), .x4(x4), .x5(x5), .x7(x7), .LD_AR(LD_AR), .INR_AR(INR_AR), .LD_PC(LD_PC),
    .INR_PC(INR_PC), .LD_DR(LD_DR), .INR_DR(INR_DR), .LD_AC(LD_AC), .INR_AC(INR_AC), .CLR_AC(CLR_AC),
    .LD_IR(LD_IR), .S(S), .y0(y0), .y1(y1), .y2(y2), .y3(y3), .y4(y4), .y5(y5), .y6(y6), .y7(y7), .IR(IR),
    .DR(DR), .AC(AC), .E(Eout), .CLK(CLK), .Memory_Enable(Memory_Enable));
  Clock Clock (.S(S), .CLK(CLK));
  ALU ALU (.AC(AC), .DR(DR), .Eout(Eout), .AC_2(ALU_ac_2), .Ein(ALU_ein), .in_4(priority_encoder_1_out));
  Priority_Encoder priority_encoder_1 (
    .in0(y0), .in1(y1), .in2(y2), .in3(y3), .in4(y4), .in5(y5), .in6(y6), .in7(y7),
    .out(priority_encoder_1_out));  // open: en_in
  _1_bit_Register E (.CLK(CLK), .INPUT(ALU_ein), .OUTPUT(Eout));
  Memory_Control Memory_Control (.BUS(bus_1_out_11), .Read(x7), .Enable(Memory_Enable), .Memory(Memory_Control_memory));
  Bit_Extender #(.in_width(16), .out_width(12)) bit_extender_1 (.in(bus_1_out_11), .out(bit_extender_1_out));
  _12_bit_Register AR (.OUT(AR_out), .INP(bit_extender_1_out), .CLK(CLK), .LD(LD_AR), .INR(INR_AR));  // open: CLR
  Bit_Extender #(.in_width(16), .out_width(12)) bit_extender_2 (.in(bus_1_out_11), .out(bit_extender_2_out));
  _12_bit_Register PC (.OUT(PC_out), .INP(bit_extender_2_out), .CLK(CLK), .LD(LD_PC), .INR(INR_PC));  // open: CLR
  _16_bit_Register u_DR (.OUT(DR), .INP(bus_1_out_11), .CLK(CLK), .LD(LD_DR), .INR(INR_DR));  // open: CLR
  _16_bit_Register u_AC (.OUT(AC), .INP(ALU_ac_2), .CLK(CLK), .CLR(CLR_AC), .LD(LD_AC), .INR(INR_AC));
  _16_bit_Register u_IR (.OUT(IR), .INP(bus_1_out_11), .CLK(CLK), .LD(LD_IR));  // open: CLR, INR
  _16_bit_Register TR (.OUT(TR_out), .INP(bus_1_out_11), .CLK(CLK));  // open: CLR, LD, INR
  RAM #(.addrWidth(12), .dataWidth(16)) ram_1 (
    .addr(AR_out), .data(Memory_Control_memory), .sel(Memory_Enable), .clk(CLK), .ld(x7));  // open: clr
  assign bit_extender_3_out = {{4{1'b0}}, AR_out};  // Bit_Extender bit_extender_3
  assign bit_extender_4_out = {{4{1'b0}}, PC_out};  // Bit_Extender bit_extender_4
  BUS bus_1 (
    .in_1(bit_extender_3_out), .in_2(bit_extender_4_out), .in_3(DR), .in_4(AC), .in_5(IR), .in_6(TR_out),
    .in_7(Memory_Control_memory), .S0(priority_encoder_2_out[0]), .S1(priority_encoder_2_out[1]),
    .S2(priority_encoder_2_out[2]), .out_11(bus_1_out_11));
  Priority_Encoder priority_encoder_2 (
    .in1(x1), .in2(x2), .in3(x3), .in4(x4), .in5(x5), .in6(x6), .in7(x7), .out(priority_encoder_2_out));  // open: in0, en_in, gs, en_out
endmodule
