// Logisim project Clock.circ as structural Verilog: 1 circuit, main circuit Clock
module Clock (
  input  S,
  output CLK
);

  wire CLK_out, not_1_out, S_qn;

  Clock_part u_CLK (.out(CLK_out));
  not not_1 (not_1_out, S);
  D_Flip_Flop u_S (.clk(CLK_out), .D(not_1_out), .Qn(S_qn), .en(S_qn));  // open: Q, preset, reset
  and and_1 (CLK, CLK_out, S_qn);
endmodule
