// Logisim project Control Unit.circ as structural Verilog: 1 circuit, main circuit Control Unit
module Control_Unit (
  input  E,
  input  [15:0] IR,
  input  [15:0] DR,
  input  [15:0] AC,
  input  CLK,
  output x1,
  output x2,
  output x3,
  output x4,
  output x5,
  output x7,
  output LD_AR,
  output INR_AR,
  output LD_PC,
  output INR_PC,
  output LD_DR,
  output INR_DR,
  output LD_AC,
  output INR_AC,
  output CLR_AC,
  output LD_IR,
  output Memory_Enable,
  output S,
  output y0,
  output y1,
  output y2,
  output y3,
  output y4,
  output y5,
  output y6,
  output y7
);

  wire and_1_out, and_2_out, and_3_out, and_4_out, and_5_out, and_8_out, and_9_out, and_13_out, and_14_out,
       and_23_out, and_25_out, and_26_out, and_27_out, and_28_out, and_29_out, and_30_out, and_32_out,
       and_33_out, and_34_out, and_35_out, and_36_out, and_37_out, CLR_SC, D0, D1, D2, D3, D4, D5, D6, D7, I,
       nor_1_out, nor_2_out, not_1_out, not_2_out, not_3_out, not_4_out, not_5_out, or_1_out, or_2_out,
       or_3_out, or_7_out, or_9_out, or_10_out, or_11_out, r, T0, T3, T4, T5, T6, T7, T8, T9, T10, T11, T12,
       T13, T14, T15;
  wire [3:0] SC_out;

  _1_bit_Register u_I (.CLK(CLK), .INPUT(IR[15]), .OUTPUT(I));
  Decoder #(.select(4), .disabled(0), .enable("false")) decoder_1 (
    .out0(T0), .out1(LD_IR), .out2(x5), .out3(T3), .out4(T4), .out5(T5), .out6(T6), .out7(T7), .out8(T8),
    .out9(T9), .out10(T10), .out11(T11), .out12(T12), .out13(T13), .out14(T14), .out15(T15), .sel(SC_out));
  Sequence_Counter SC (.OUT(SC_out), .CLK(CLK), .CLR(CLR_SC), .INR(1'b1));
  Decoder #(.select(3), .disabled(0), .enable("false")) decoder_2 (
    .out0(D0), .out1(D1), .out2(D2), .out3(D3), .out4(D4), .out5(D5), .out6(D6), .out7(D7), .sel(IR[14:12]));
  and and_1 (and_1_out, D4, T4);
  and and_2 (and_2_out, D5, T5);
  and and_3 (and_3_out, D5, T4);
  and and_4 (and_4_out, D2, T5);
  and and_5 (and_5_out, D6, T6);
  and and_6 (x4, D3, T4);
  not not_1 (not_1_out, D7);
  not not_2 (not_2_out, I);
  not not_3 (not_3_out, D7);
  and and_7 (INR_AR, D5, T4);
  and and_8 (and_8_out, D4, T4);
  and and_9 (and_9_out, D5, T5);
  not not_4 (not_4_out, AC[15]);
  and and_10 (INR_DR, D6, T5);
  and and_11 (INR_AC, r, IR[5]);
  and and_12 (CLR_AC, r, IR[11]);
  or or_1 (or_1_out, D3, D5);
  and and_13 (and_13_out, D6, T6);
  or or_2 (or_2_out, D3, D4);
  or or_3 (or_3_out, D0, D1, D2, D5);
  and and_14 (and_14_out, D6, T6);
  and and_15 (y0, D0, T5);
  and and_16 (y1, D1, T5);
  and and_17 (y2, D2, T5);
  and and_18 (y3, r, IR[9]);
  and and_19 (y4, r, IR[7]);
  and and_20 (y5, r, IR[6]);
  and and_21 (y6, r, IR[10]);
  and and_22 (y7, r, IR[8]);
  or or_4 (x1, and_1_out, and_2_out);
  or or_5 (x2, and_3_out, T0);
  or or_6 (x3, and_4_out, and_5_out);
  or or_7 (or_7_out, D0, D1, D2, D6);
  and and_23 (and_23_out, not_1_out, I, T3);
  and and_24 (r, D7, not_2_out, T3);
  and and_25 (and_25_out, not_3_out, I, T3);
  or or_8 (LD_PC, and_8_out, and_9_out);
  nor nor_1 (nor_1_out, DR[0], DR[1], DR[2], DR[3], DR[4], DR[5], DR[6], DR[7], DR[9], DR[10], DR[11], DR[12], DR[13], DR[14], DR[15], DR[8]);
  nor nor_2 (nor_2_out, AC[0], AC[1], AC[2], AC[3], AC[4], AC[5], AC[6], AC[7], AC[9], AC[10], AC[11], AC[12], AC[13], AC[14], AC[15], AC[8]);
  not not_5 (not_5_out, E);
  or or_9 (or_9_out, D0, D1, D2, D6);
  or or_10 (or_10_out, D0, D1, D2);
  or or_11 (or_11_out, IR[6], IR[7], IR[9]);
  nand nand_1 (S, r, IR[0]);
  and and_26 (and_26_out, or_7_out, T4);
  or or_12 (LD_AR, and_25_out, T0, x5);
  and and_27 (and_27_out, r, IR[2], nor_2_out);
  and and_28 (and_28_out, r, IR[4], not_4_out);
  and and_29 (and_29_out, r, IR[3], AC[15]);
  and and_30 (and_30_out, r, IR[1], not_5_out);
  and and_31 (LD_DR, or_9_out, T4);
  and and_32 (and_32_out, or_10_out, T5);
  and and_33 (and_33_out, or_11_out, r);
  and and_34 (and_34_out, or_1_out, T4);
  and and_35 (and_35_out, or_2_out, T4);
  and and_36 (and_36_out, or_3_out, T5);
  and and_37 (and_37_out, D6, T6, nor_1_out);
  or or_13 (x7, and_26_out, LD_IR, and_23_out);
  or or_14 (LD_AC, and_32_out, and_33_out);
  or or_15 (Memory_Enable, and_34_out, and_13_out, x7);
  or or_16 (CLR_SC, and_35_out, and_36_out, and_14_out, r);
  or or_17 (INR_PC, LD_IR, and_37_out, and_27_out, and_28_out, and_29_out, and_30_out);

  // Other names for the same wires on the sheet: B0 = IR[0]; B1 = IR[1]; B2 = IR[2]; B3 = IR[3]; B4 = IR[4];
  //   B5 = IR[5]; B6 = IR[6]; B7 = IR[7]; B8 = IR[8]; B9 = IR[9]; B10 = IR[10]; B11 = IR[11]; Memory_Read = x7;
  //   T1 = LD_IR; T2 = x5
endmodule
