// Logisim project Memory Control.circ as structural Verilog: 1 circuit, main circuit Memory Control
module Memory_Control (
  input  [15:0] BUS,
  input  Read,
  input  Enable,
  output [15:0] Memory
);

  wire and_1_out, not_1_out;

  not not_1 (not_1_out, Read);
  and and_1 (and_1_out, not_1_out, Enable);
  Multiplexer #(.width(16), .enable("false")) multiplexer_1 (.in1(BUS), .out(Memory), .sel(and_1_out));  // open: in0
endmodule
