// Logisim project Sequence Counter.circ as structural Verilog: 1 circuit, main circuit Sequence Counter
module Sequence_Counter (
  input  INR,
  input  CLK,
  input  CLR,
  output [3:0] OUT
);

  wire d_ff_1_q;

  Pull_Resistor pull_resistor_1 (.node(INR));
  Counter #(.width(4), .max('hf)) counter_1 (.count(INR), .Q(OUT), .clk(CLK), .clr(d_ff_1_q));  // open: load, D, carry
  D_Flip_Flop d_ff_1 (.clk(CLK), .D(CLR), .Q(d_ff_1_q), .reset(d_ff_1_q));  // open: Qn, preset, en
  Pull_Resistor pull_resistor_2 (.node(CLR));
endmodule
